# Fritzing sketch led-flex-joystick (saved by Fritzing 0.9.10b)
breadboards: 1
stripboards: 1

parts:
  부품1 = Arduino Uno (Rev3)
  R1 = Resistor [tolerance=±5% power=0.25 resistance=47k package=THT]
  R2 = 2.2 inch Basic Flex Resistor
  U1 = JOYSTICK-PSP1000 [package=joystick-psp1000]
  LED1 = LED - 5mm [color="Red (633nm)" current=0.030 package="5 mm [THT]"]
  LED2 = LED - 5mm [color="Red (633nm)" current=0.030 package="5 mm [THT]"]
  LED3 = LED - 5mm [color="Red (633nm)" current=0.030 package="5 mm [THT]"]
  LED4 = LED - 5mm [color="Red (633nm)" current=0.030 package="5 mm [THT]"]
  LED5 = LED - 5mm [color="Red (633nm)" current=0.030 package="5 mm [THT]"]
  R3 = Resistor [tolerance=±5% power=0.25 resistance=220 package=THT]
  R4 = Resistor [tolerance=±5% power=0.25 resistance=220 package=THT]
  R5 = Resistor [tolerance=±5% power=0.25 resistance=220 package=THT]
  R6 = Resistor [tolerance=±5% power=0.25 resistance=220 package=THT]
  R7 = Resistor [tolerance=±5% power=0.25 resistance=220 package=THT]

nets:
  N1: 부품1.A0, U1.Y
  N2: 부품1.A2, R1.Pin_1, R2.Pin_2
  N3: 부품1.D9_PWM, R5.Pin_0
  N4: 부품1.D10_PWM/SS, R6.Pin_0
  N5: 부품1.D11_PWM/MOSI, R7.Pin_0
  N6: 부품1.D5_PWM, R3.Pin_0
  N7: 부품1.D6_PWM, R4.Pin_0
  N8: 부품1.5V, R2.pin_1, U1.X
  N9: 부품1.GND, R1.Pin_0, LED1.anode, LED2.anode, LED3.anode, LED4.anode, LED5.anode
  N10: LED1.cathode, R3.Pin_1
  N11: LED2.cathode, R4.Pin_1
  N12: LED3.cathode, R5.Pin_1
  N13: LED4.cathode, R6.Pin_1
  N14: LED5.cathode, R7.Pin_1

custom parts:
  2.2 inch Basic Flex Resistor: A generic Flex resistor - SparkFun: SEN-10264
